# Fritzing sketch HypnoLight (saved by Fritzing 0.9.5d)

parts:
  Power_RGB1 = Prolight RGB 3 Watt Star
  M1 = ESP32-S3-DevKitC-1-N8R8-v1 [part_number=ESP32-S3-DevKitC-1-N8R8-v1]
  Part1 = PicoBuck LED Driver [part_number=COM-11850]
  Part2 = PicoBuck LED Driver [part_number=COM-11850]
  Part3 = PicoBuck LED Driver [part_number=COM-11850]
  J1 = Screw terminal - 2 pins [package=THT]
  Power_RGB2 = Prolight RGB 3 Watt Star
  Power_RGB3 = Prolight RGB 3 Watt Star
  Adafruit_I2C_Quad_Rotary_Encoder_Breakout1 = Adafruit I2C Quad Rotary Encoder Breakout [part_number=#5752]
  OLED_I2C1 = OLED 128x64 I2C Monochrome Display

nets:
  N1: Power_RGB1.R+, Part1.OUT1+
  N2: Power_RGB1.R-, Part1.OUT1-
  VCC: M1.pin_1, Adafruit_I2C_Quad_Rotary_Encoder_Breakout1.VCC, OLED_I2C1.VDD
  N3: M1.pin_5, Part1.IN1
  N4: M1.pin_6, Part1.IN2
  N5: M1.pin_7, Part1.IN3
  N6: M1.pin_8, Part2.IN1
  N7: M1.pin_9, Part2.IN2
  N8: M1.pin_10, Part2.IN3
  N9: M1.pin_11, Part3.IN1
  N10: M1.pin_12, Part3.IN2
  N11: M1.pin_13, Part3.IN3
  GND: M1.pin_22, M1.pin_24, M1.pin_44, Part1.GND, Part2.GND, Part3.GND, Adafruit_I2C_Quad_Rotary_Encoder_Breakout1.GND, OLED_I2C1.GND
  N12: M1.pin_34, Adafruit_I2C_Quad_Rotary_Encoder_Breakout1.SCL, OLED_I2C1.SDA
  N13: M1.pin_35, Adafruit_I2C_Quad_Rotary_Encoder_Breakout1.SDA, OLED_I2C1.SCK
  N14: Part1.VIN_+, J1.pin1
  N15: Part1.VIN_-, Part2.VIN_-, Part3.VIN_-, J1.pin2
  N16: Part1.OUT2+, Power_RGB3.R+
  N17: Part1.OUT2-, Power_RGB3.R-
  N18: Part1.OUT3+, Power_RGB2.R+
  N19: Part1.OUT3-, Power_RGB2.R-

custom parts:
  ESP32-S3-DevKitC-1-N8R8-v1: ESP32-S3-DevKitC-1-N8R8-v1 This module is 44pins long (2x22) and 11 pins width.
  PicoBuck LED Driver: The PicoBuck LED Driver is an economical and easy to use driver that will allow you to control and blend three different LEDs on three different channels. Power in supplied to the PicoBuck with a wide range of input voltages (6v to 20v) connected to the VIN header and three inputs for each driver channel (labeled IN1, IN2, and IN3) driven with standard 3.3v or 5v logic. This PicoBuck supports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
  Adafruit I2C Quad Rotary Encoder Breakout: Rotary encoders are soooo much fun! Twist em this way, then twist them that way. Unlike potentiometers, they go all the way around and often have little detents for tactile feedback. But, if you've ever tried to add encoders to your project you know that they're a real challenge to use: timers, interrupts, debouncing... This Stemma QT breakout makes all that frustration go away - and allows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
